# Fritzing sketch fritzing-Sketch (saved by Fritzing 0.9.4)
breadboards: 1

parts:
  LED1 = LED - 5mm [color="Red (633nm)" package="5 mm [THT]"]
  LED2 = LED - 5mm [color="Green (555nm)" package="5 mm [THT]"]
  DHT1 = DHT22 Humidity and Temperature Sensor
  R1 = Resistor [tolerance=±5% resistance=220 package=THT]
  R2 = Resistor [tolerance=±5% resistance=220 package=THT]
  U1 = NodeMCU V3.0
  Grove1 = Grove OLED 128x96
  DS1 = DS18B20 1-Wire Temperature Sensor [part_number=DS18B20]

nets:
  GND: LED1.cathode, LED2.cathode, DHT1.GND, U1.GND#6, U1.GND#13, U1.GND#16, U1.GND#33, Grove1.GND, DS1.GND
  N1: LED1.anode, R2.Pin_0
  N2: LED2.anode, R1.Pin_0
  VDD: DHT1.VDD, U1.3V3, Grove1.VCC, DS1.VDD
  N3: DHT1.DATA, U1.D5
  N4: R1.Pin_1, U1.D6
  N5: R2.Pin_1, U1.D7
  N6: U1.D1, Grove1.SCL
  N7: U1.D2, Grove1.SDA
  N8: U1.D4, DS1.DQ

custom parts:
  NodeMCU V3.0: ESP8266 based NodeMCU
